# Fritzing sketch wiring (saved by Fritzing 0.9.3b)

parts:
  Part1 = Adafruit Feather M4 Express [part_number="Adafruit #3857"]
  Part2 = Adafruit Feather M4 Express [part_number="Adafruit #3857"]
  R2 = Trimmer Potentiometer [maximum_resistance=10kΩ package=THT]
  LED2 = smd LED [color="Red (633nm)" package="1206 [SMD]"]
  R4 = Resistor [tolerance=±5% resistance=220 package=THT]
  S1 = Momentary Switch [package=ksa_sealed_tac_switch]

nets:
  N1: Part1.GND, S1.2
  N2: Part1.D12, S1.3
  N3: Part2.A1, LED2.anode
  N4: Part2.A0, R2.wiper
  N5: Part2.GND, R2.leg1, R4.Pin_0
  N6: Part2.+3V3, R2.leg2

custom parts:
  Adafruit Feather M4 Express: It's what you've been waiting for, the Feather M4 Express featuring ATSAMD51. This Feather is fast like a swift, smart like an owl, strong like a ox-bird (it's half ox, half bird, OK?) This feather is powered by our new favorite chip, the ATSAMD51J19 - with its 120MHz Cortex M4 with floating point support and 512KB Flash and 192KB RAM. Your code will zig and zag and zoom, and with a bunch of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
